// Logisim project pract_1.circ as structural Verilog
module main (
  input  A,
  input  B,
  input  E
);

  wire decoder_2_1_out_4, decoder_2_1_out_5, decoder_2_1_out_6, decoder_2_1_out_7;

  decoder_2 decoder_2_1 (
    .a(A), .b(B), .e(E), .out_4(decoder_2_1_out_4), .out_5(decoder_2_1_out_5), .out_6(decoder_2_1_out_6),
    .out_7(decoder_2_1_out_7));
  LED led_1 (.in(decoder_2_1_out_4));
  LED led_2 (.in(decoder_2_1_out_5));
  LED led_3 (.in(decoder_2_1_out_6));
  LED led_4 (.in(decoder_2_1_out_7));
endmodule

module decoder_2 (
  input  a,
  input  b,
  input  e,
  output out_4,
  output out_5,
  output out_6,
  output out_7
);

  wire not_1_out, not_2_out, not_3_out, not_4_out;

  not not_1 (not_1_out, a);
  not not_2 (not_2_out, b);
  and and_1 (out_4, not_1_out, not_2_out, e);
  not not_3 (not_3_out, b);
  and and_2 (out_5, a, not_3_out, e);
  not not_4 (not_4_out, a);
  and and_3 (out_6, not_4_out, b, e);
  and and_4 (out_7, b, a, e);
endmodule

module decoder_3 (
  input  C,
  input  B,
  input  A,
  input  E,
  output out_5,
  output out_6,
  output out_7,
  output out_8,
  output out_9,
  output out_10,
  output out_11,
  output out_12
);

  wire and_1_out, and_2_out, not_1_out;

  and and_1 (and_1_out, E, not_1_out);
  not not_1 (not_1_out, C);
  and and_2 (and_2_out, E, C);
  decoder_2 decoder_2_1 (.a(A), .b(B), .e(and_1_out), .out_4(out_5), .out_5(out_6), .out_6(out_7), .out_7(out_8));
  decoder_2 decoder_2_2 (.a(A), .b(B), .e(and_2_out), .out_4(out_9), .out_5(out_10), .out_6(out_11), .out_7(out_12));
endmodule

// VHDL entity test, as the project stores it:
--------------------------------------------------------------------------------
-- Project :
-- File    :
-- Autor   :
-- Date    :
--
--------------------------------------------------------------------------------
-- Description :
--
--------------------------------------------------------------------------------

LIBRARY ieee;
USE ieee.std_logic_1164.all;

ENTITY test IS
  PORT (
  ------------------------------------------------------------------------------
  --Insert input ports below
    clock      : IN  std_logic;                    -- input bit example
    val        : IN  std_logic_vector(3 DOWNTO 0); -- input vector example
  ------------------------------------------------------------------------------
  --Insert output ports below
    max        : OUT std_logic;                    -- output bit example
    cpt        : OUT std_logic_vector(3 DOWNTO 0)  -- output vector example
    );
END test;

--------------------------------------------------------------------------------
--Complete your VHDL description below
--------------------------------------------------------------------------------

ARCHITECTURE TypeArchitecture OF test IS

BEGIN


END TypeArchitecture;
